// Logisim project 4x4 podlonczenie.circ as structural Verilog: 1 circuit, main circuit main
module main (
  input  in_1,
  input  in_2,
  input  in_3,
  input  in_4,
  input  [4:0] in_5,
  input  in_6,
  input  in_7,
  input  in_8,
  input  in_9,
  input  in_10,
  input  in_11,
  input  in_12,
  input  in_13,
  input  in_14,
  input  [4:0] in_15,
  input  in_16,
  input  in_17,
  input  in_18,
  input  in_19,
  input  [3:0] in_20,
  input  [3:0] in_21,
  input  [3:0] in_22,
  input  in_23,
  input  [3:0] in_24,
  input  [3:0] in_25
);

  wire clock_1_out;
  wire [3:0] adder_1_out, main_1_out_25, main_1_out_29, main_1_out_33, main_1_out_37;

  Adder #(.width(1)) adder_1 (.a(in_24[0]), .b(in_25[0]), .out(adder_1_out[0]));  // open: cin, cout
  Clock clock_1 (.out(clock_1_out));
  Adder #(.width(1)) adder_2 (.a(in_24[1]), .b(in_25[1]), .out(adder_1_out[1]));  // open: cin, cout
  Adder #(.width(1)) adder_3 (.a(in_24[2]), .b(in_25[2]), .out(adder_1_out[2]));  // open: cin, cout
  Test_4x4_main main_1 (
    .When_Gets_Lonely(in_20), .When_Gets_Alive(in_21), .When_Gets_Overcroweded(in_22), .in_4(in_1),
    .in_8(in_7), .in_12(in_11), .in_16(in_16), .in_5(in_2), .in_9(in_8), .in_13(in_12), .in_17(in_17),
    .in_6(in_3), .in_10(in_9), .in_14(in_13), .in_18(in_18), .in_7(in_4), .in_11(in_10), .in_15(in_14),
    .in_19(in_19), .Clock(clock_1_out), .Clock_Anabler_Stop(in_23), .out_22(main_1_out_25[3]),
    .out_23(main_1_out_25[2]), .out_24(main_1_out_25[1]), .out_25(main_1_out_25[0]),
    .out_26(main_1_out_29[3]), .out_27(main_1_out_29[2]), .out_28(main_1_out_29[1]),
    .out_29(main_1_out_29[0]), .out_30(main_1_out_33[3]), .out_31(main_1_out_33[2]),
    .out_32(main_1_out_33[1]), .out_33(main_1_out_33[0]), .out_34(main_1_out_37[3]),
    .out_35(main_1_out_37[2]), .out_36(main_1_out_37[1]), .out_37(main_1_out_37[0]));
  Adder #(.width(1)) adder_4 (.a(in_24[3]), .b(in_25[3]), .out(adder_1_out[3]));  // open: cin, cout
  DotMatrix #(.inputtype("row"), .matrixcols(4), .matrixrows(1)) dotmatrix_1 (.row0(adder_1_out));
  DotMatrix #(.inputtype("row"), .matrixcols(4), .matrixrows(4)) dotmatrix_2 (
    .row0(main_1_out_25), .row1(main_1_out_29), .row2(main_1_out_33), .row3(main_1_out_37));
endmodule
