// Logisim project Ekran.circ as structural Verilog: 1 circuit, main circuit main
module main (
  input  [31:0] in_1
);

  wire clock_1_out, comparator_1_gt, comparator_1_lt, keyboard_1_avail, main_2_p2, register_1_q;
  wire [4:0] main_1_out_2, main_1_out_3, main_2_p3;
  wire [6:0] keyboard_1_data;
  wire [7:0] counter_1_q;
  wire [31:0] adder_1_out, main_3_out_3, main_3_out_4, main_3_out_5, main_3_out_6, main_3_out_7,
       main_3_out_8, main_3_out_9, main_3_out_10, main_3_out_11, main_3_out_12, main_3_out_13, main_3_out_14,
       main_3_out_15, main_3_out_16, main_3_out_17, main_3_out_18, main_3_out_19, main_3_out_20,
       main_3_out_21, main_3_out_22, main_3_out_23, main_3_out_24, main_3_out_25, main_3_out_26,
       main_3_out_27, main_3_out_28, main_3_out_29, main_3_out_30, main_3_out_31, main_3_out_32,
       main_3_out_33, main_3_out_34, main_4_out_65, main_4_out_66, main_4_out_67, main_4_out_68,
       main_4_out_69, main_4_out_70, main_4_out_71, main_4_out_72, main_4_out_73, main_4_out_74,
       main_4_out_75, main_4_out_76, main_4_out_77, main_4_out_78, main_4_out_79, main_4_out_80,
       main_4_out_81, main_4_out_82, main_4_out_83, main_4_out_84, main_4_out_85, main_4_out_86,
       main_4_out_87, main_4_out_88, main_4_out_89, main_4_out_90, main_4_out_91, main_4_out_92,
       main_4_out_93, main_4_out_94, main_4_out_95, main_4_out_96, shifter_1_out, shifter_2_out;

  Keyboard keyboard_1 (.re(1'b1), .clr(register_1_q), .avail(keyboard_1_avail), .data(keyboard_1_data));  // open: clk
  Clock clock_1 (.out(clock_1_out));
  Register #(.width(1)) register_1 (.D(keyboard_1_avail), .Q(register_1_q), .clk(clock_1_out));  // open: en, clr
  Register #(.width(7)) register_2 (.D(keyboard_1_data), .clk(clock_1_out));  // open: en, Q, clr
  Counter counter_1 (.Q(counter_1_q), .clk(clock_1_out));  // open: load, D, count, carry, clr
  Comparator comparator_1 (.a(counter_1_q), .b(8'hc8), .gt(comparator_1_gt), .lt(comparator_1_lt));  // open: eq
  LR_main main_1 (.in_1(keyboard_1_data), .out_2(main_1_out_2), .out_3(main_1_out_3));
  // Enter_Up_Down_main main_2: pin names not known; wires that end beside it: keyboard_1_data, main_2_p2, main_2_p3
  Shifter #(.width(32)) shifter_1 (.in(32'h8000), .\dist (main_1_out_2), .out(shifter_1_out));
  Shifter #(.width(32), .shift("lr")) shifter_2 (.in(shifter_1_out), .\dist (main_1_out_3), .out(shifter_2_out));
  Adder #(.width(32)) adder_1 (.a({32{1'b0}}), .b(shifter_2_out), .out(adder_1_out));  // open: cin, cout
  Uu_Down32_main main_3 (
    .in_1(main_2_p3), .in_2(adder_1_out), .out_3(main_3_out_3), .out_4(main_3_out_4), .out_5(main_3_out_5),
    .out_6(main_3_out_6), .out_7(main_3_out_7), .out_8(main_3_out_8), .out_9(main_3_out_9),
    .out_10(main_3_out_10), .out_11(main_3_out_11), .out_12(main_3_out_12), .out_13(main_3_out_13),
    .out_14(main_3_out_14), .out_15(main_3_out_15), .out_16(main_3_out_16), .out_17(main_3_out_17),
    .out_18(main_3_out_18), .out_19(main_3_out_19), .out_20(main_3_out_20), .out_21(main_3_out_21),
    .out_22(main_3_out_22), .out_23(main_3_out_23), .out_24(main_3_out_24), .out_25(main_3_out_25),
    .out_26(main_3_out_26), .out_27(main_3_out_27), .out_28(main_3_out_28), .out_29(main_3_out_29),
    .out_30(main_3_out_30), .out_31(main_3_out_31), .out_32(main_3_out_32), .out_33(main_3_out_33),
    .out_34(main_3_out_34));
  DotMatrix #(.inputtype("row"), .matrixcols(32), .matrixrows(32)) dotmatrix_1 (
    .row0(main_4_out_65), .row1(main_4_out_66), .row2(main_4_out_67), .row3(main_4_out_68),
    .row4(main_4_out_69), .row5(main_4_out_70), .row6(main_4_out_71), .row7(main_4_out_72),
    .row8(main_4_out_73), .row9(main_4_out_74), .row10(main_4_out_75), .row11(main_4_out_76),
    .row12(main_4_out_77), .row13(main_4_out_78), .row14(main_4_out_79), .row15(main_4_out_80),
    .row16(main_4_out_81), .row17(main_4_out_82), .row18(main_4_out_83), .row19(main_4_out_84),
    .row20(main_4_out_85), .row21(main_4_out_86), .row22(main_4_out_87), .row23(main_4_out_88),
    .row24(main_4_out_89), .row25(main_4_out_90), .row26(main_4_out_91), .row27(main_4_out_92),
    .row28(main_4_out_93), .row29(main_4_out_94), .row30(main_4_out_95), .row31(main_4_out_96));
  Register32x32_main main_4 (
    .in_1(main_3_out_3), .in_2(main_3_out_4), .in_3(main_3_out_5), .in_4(main_3_out_6), .in_5(main_3_out_7),
    .in_6(main_3_out_8), .in_7(main_3_out_9), .in_8(main_3_out_10), .in_9(main_3_out_11),
    .in_10(main_3_out_12), .in_11(main_3_out_13), .in_12(main_3_out_14), .in_13(main_3_out_15),
    .in_14(main_3_out_16), .in_15(main_3_out_17), .in_16(main_3_out_18), .in_17(main_3_out_19),
    .in_18(main_3_out_20), .in_19(main_3_out_21), .in_20(main_3_out_22), .in_21(main_3_out_23),
    .in_22(main_3_out_24), .in_23(main_3_out_25), .in_24(main_3_out_26), .in_25(main_3_out_27),
    .in_26(main_3_out_28), .in_27(main_3_out_29), .in_28(main_3_out_30), .in_29(main_3_out_31),
    .in_30(main_3_out_32), .in_31(main_3_out_33), .in_32(main_3_out_34), .in_33(in_1), .in_34(in_1),
    .in_35(in_1), .in_36(in_1), .in_37(in_1), .in_38(in_1), .in_39(in_1), .in_40(in_1), .in_41(in_1),
    .in_42(in_1), .in_43(in_1), .in_44(in_1), .in_45(in_1), .in_46(in_1), .in_47(in_1), .in_48(in_1),
    .in_49(in_1), .in_50(in_1), .in_51(in_1), .in_52(in_1), .in_53(in_1), .in_54(in_1), .in_55(in_1),
    .in_56(in_1), .in_57(in_1), .in_58(in_1), .in_59(in_1), .in_60(in_1), .in_61(in_1), .in_62(in_1),
    .in_63(in_1), .in_64(in_1), .out_65(main_4_out_65), .out_66(main_4_out_66), .out_67(main_4_out_67),
    .out_68(main_4_out_68), .out_69(main_4_out_69), .out_70(main_4_out_70), .out_71(main_4_out_71),
    .out_72(main_4_out_72), .out_73(main_4_out_73), .out_74(main_4_out_74), .out_75(main_4_out_75),
    .out_76(main_4_out_76), .out_77(main_4_out_77), .out_78(main_4_out_78), .out_79(main_4_out_79),
    .out_80(main_4_out_80), .out_81(main_4_out_81), .out_82(main_4_out_82), .out_83(main_4_out_83),
    .out_84(main_4_out_84), .out_85(main_4_out_85), .out_86(main_4_out_86), .out_87(main_4_out_87),
    .out_88(main_4_out_88), .out_89(main_4_out_89), .out_90(main_4_out_90), .out_91(main_4_out_91),
    .out_92(main_4_out_92), .out_93(main_4_out_93), .out_94(main_4_out_94), .out_95(main_4_out_95),
    .out_96(main_4_out_96));
endmodule
