// Logisim project Enter_Up_Down.circ as structural Verilog: 1 circuit, main circuit main
module main (
  input  [6:0] in_1,
  input  in_2,
  output out_3,
  output [4:0] out_4,
  output out_5,
  output out_6
);

  wire and_1_out, comparator_1_eq, comparator_2_eq, comparator_3_eq, comparator_5_eq, comparator_6_gt,
       comparator_6_lt, counter_2_carry, or_1_out, or_2_out;

  Comparator #(.width(7)) comparator_1 (.a(in_1), .b(7'b0001010), .eq(comparator_1_eq));  // open: gt, lt
  Comparator #(.width(7)) comparator_2 (.a(in_1), .b(7'b1110111), .eq(comparator_2_eq));  // open: gt, lt
  Comparator #(.width(7)) comparator_3 (.a(in_1), .b(7'b1110011), .eq(comparator_3_eq));  // open: gt, lt
  Comparator #(.width(7)) comparator_4 (.a(in_1), .b(7'b1110010), .eq(out_5));  // open: gt, lt
  Comparator #(.width(7)) comparator_5 (.a(in_1), .b(7'b0100000), .eq(comparator_5_eq));  // open: gt, lt
  and and_1 (and_1_out, comparator_3_eq, or_2_out);
  Counter #(.width(1), .max('h1)) counter_1 (.Q(out_6), .clk(comparator_5_eq));  // open: load, D, count, carry, clr
  Counter #(.max('h4)) counter_2 (.carry(counter_2_carry), .clk(in_2));  // open: load, D, count, Q, clr
  Counter #(.width(5), .max('h13), .ongoal("stay")) counter_3 (
    .load(comparator_3_eq), .count(1'b1), .Q(out_4), .clk(or_1_out));  // open: D, carry, clr
  or or_1 (or_1_out, comparator_2_eq, and_1_out);
  Register #(.width(1)) register_1 (
    .D(comparator_1_eq), .Q(out_3), .clk(comparator_1_eq), .clr(counter_2_carry));  // open: en
  or or_2 (or_2_out, comparator_6_gt, comparator_6_lt);
  Comparator #(.width(5)) comparator_6 (
    .a(out_4), .b({5{1'b0}}), .gt(comparator_6_gt), .lt(comparator_6_lt));  // open: eq
endmodule
