// Logisim project LR.circ as structural Verilog: 1 circuit, main circuit main
module main (
  input  [6:0] in_1,
  output [4:0] out_2,
  output [4:0] out_3
);

  wire and_1_out, and_2_out, and_3_out, and_4_out, and_5_out, comparator_1_eq, comparator_2_eq,
       comparator_3_eq, comparator_3_gt, comparator_4_eq, comparator_4_gt, counter_1_carry, counter_2_carry,
       or_1_out, or_2_out, or_3_out, or_4_out, or_5_out, or_6_out, or_7_out;

  Comparator #(.width(7)) comparator_1 (.a(in_1), .b(7'b1100001), .eq(comparator_1_eq));  // open: gt, lt
  Comparator #(.width(7)) comparator_2 (.a(in_1), .b(7'b1100100), .eq(comparator_2_eq));  // open: gt, lt
  Counter #(.width(5), .max('h10), .ongoal("stay")) counter_1 (
    .load(or_7_out), .D(5'b10000), .count(1'b1), .Q(out_2), .carry(counter_1_carry), .clk(or_5_out));  // open: clr
  Counter #(.width(5), .max('hf), .ongoal("stay")) counter_2 (
    .load(or_7_out), .D(5'b01111), .count(1'b1), .Q(out_3), .carry(counter_2_carry), .clk(or_6_out));  // open: clr
  Comparator #(.width(5)) comparator_3 (
    .a(out_2), .b({5{1'b0}}), .gt(comparator_3_gt), .eq(comparator_3_eq));  // open: lt
  and and_1 (and_1_out, or_3_out, comparator_1_eq);
  or or_1 (or_1_out, counter_2_carry, comparator_4_gt);
  Comparator #(.width(5)) comparator_4 (
    .a(out_3), .b({5{1'b0}}), .gt(comparator_4_gt), .eq(comparator_4_eq));  // open: lt
  or or_2 (or_2_out, counter_1_carry, comparator_3_gt);
  or or_3 (or_3_out, or_2_out, and_2_out);
  and and_2 (and_2_out, comparator_3_eq, comparator_4_eq);
  or or_4 (or_4_out, or_1_out, and_2_out);
  or or_5 (or_5_out, and_1_out, and_4_out);
  and and_3 (and_3_out, or_4_out, comparator_2_eq);
  or or_6 (or_6_out, and_3_out, and_5_out);
  and and_4 (and_4_out, or_2_out, comparator_2_eq);
  and and_5 (and_5_out, comparator_1_eq, or_1_out);
  or or_7 (or_7_out, and_4_out, and_5_out);
endmodule
