// Logisim project Logika komurki koniec.circ as structural Verilog: 1 circuit, main circuit main
module main (
  input  [3:0] Cell_is_born_when__x,
  input  in_2,
  input  in_3,
  input  in_4,
  input  in_5,
  input  CLK,
  input  in_7,
  input  in_8,
  input  in_9,
  input  CLK_enabler,
  input  in_11,
  input  [3:0] Overcrowded_when__x,
  input  [3:0] Cell_gets_onely_when___x,
  input  OverwritePin,
  output Actual_State
);

  wire adder_1_out, and_1_out, and_2_out, bitfinder_1_found, comparator_1_eq, comparator_2_gt,
       comparator_3_lt, counter_1_q, d_ff_1_q, d_ff_2_q, multiplexer_1_out, nor_1_out;
  wire [3:0] bitadder_1_out, counter_2_q;

  BitAdder #(.width(1)) bitadder_1 (
    .in0(in_2), .in1(in_3), .in2(in_4), .in3(in_5), .in4(in_7), .in5(in_8), .in6(in_9), .in7(in_11),
    .out(bitadder_1_out));
  Comparator #(.width(4)) comparator_1 (
    .a(bitadder_1_out), .b(Cell_is_born_when__x), .eq(comparator_1_eq));  // open: gt, lt
  Comparator #(.width(4)) comparator_2 (
    .a(bitadder_1_out), .b(Overcrowded_when__x), .gt(comparator_2_gt));  // open: eq, lt
  Comparator #(.width(4)) comparator_3 (
    .a(bitadder_1_out), .b(Cell_gets_onely_when___x), .lt(comparator_3_lt));  // open: gt, eq
  and and_1 (and_1_out, comparator_1_eq, ~Actual_State);  // AND_Gate
  nor nor_1 (nor_1_out, comparator_2_gt, comparator_3_lt);
  Multiplexer #(.enable("false")) multiplexer_1 (
    .in0(and_1_out), .in1(nor_1_out), .out(multiplexer_1_out), .sel(Actual_State));
  D_Flip_Flop d_ff_1 (.clk(and_2_out), .D(multiplexer_1_out), .Q(d_ff_1_q));  // open: Qn, preset, en, reset
  Adder #(.width(1)) adder_1 (.a(d_ff_1_q), .b(counter_1_q), .out(adder_1_out));  // open: cin, cout
  Counter #(.width(1), .max('h1), .ongoal("load")) counter_1 (
    .Q(counter_1_q), .clk(OverwritePin), .clr(and_2_out));  // open: load, D, count, carry
  Multiplexer #(.enable("false")) multiplexer_2 (
    .in0(d_ff_1_q), .in1(d_ff_2_q), .out(Actual_State), .sel(bitfinder_1_found));
  D_Flip_Flop #(.trigger("high")) d_ff_2 (
    .clk(OverwritePin), .D(adder_1_out), .Q(d_ff_2_q));  // open: Qn, preset, en, reset
  BitFinder #(.width(4)) bitfinder_1 (.in(counter_2_q), .found(bitfinder_1_found));  // open: index
  Counter #(.width(4), .max('hf)) counter_2 (
    .Q(counter_2_q), .clk(OverwritePin), .clr(and_2_out));  // open: load, D, count, carry
  and and_2 (and_2_out, CLK, CLK_enabler);

  // Notes on the sheet:
  //   State of neighber cells
endmodule
