// Logisim project Logika komurki prawie koniec.circ as structural Verilog: 1 circuit, main circuit main
module main (
  input  in_1,
  input  in_2,
  input  in_3,
  input  in_4,
  input  in_5,
  input  in_6,
  input  in_7,
  input  in_8,
  input  in_9,
  input  in_10,
  output [3:0] out_11,
  output Actual_State
);

  wire adder_1_out, and_1_out, and_2_out, bitfinder_1_found, clock_1_out, comparator_1_eq, comparator_2_gt,
       comparator_3_lt, counter_1_q, d_ff_1_q, d_ff_2_q, multiplexer_1_out, nor_1_out;
  wire [3:0] counter_2_q;

  BitAdder #(.width(1)) bitadder_1 (
    .in0(in_1), .in1(in_2), .in2(in_3), .in3(in_4), .in4(in_5), .in5(in_6), .in6(in_7), .in7(in_9),
    .out(out_11));
  Comparator #(.width(4)) comparator_1 (.a(out_11), .b(4'b0011), .eq(comparator_1_eq));  // open: gt, lt
  Comparator #(.width(4)) comparator_2 (.a(out_11), .b(4'b0011), .gt(comparator_2_gt));  // open: eq, lt
  Comparator #(.width(4)) comparator_3 (.a(out_11), .b(4'b0010), .lt(comparator_3_lt));  // open: gt, eq
  and and_1 (and_1_out, comparator_1_eq, ~Actual_State);  // AND_Gate
  nor nor_1 (nor_1_out, comparator_2_gt, comparator_3_lt);
  Multiplexer #(.enable("false")) multiplexer_1 (
    .in0(and_1_out), .in1(nor_1_out), .out(multiplexer_1_out), .sel(Actual_State));
  D_Flip_Flop d_ff_1 (.clk(and_2_out), .D(multiplexer_1_out), .Q(d_ff_1_q));  // open: Qn, preset, en, reset
  Adder #(.width(1)) adder_1 (.a(d_ff_1_q), .b(counter_1_q), .out(adder_1_out));  // open: cin, cout
  Counter #(.width(1), .max('h1), .ongoal("load")) counter_1 (
    .Q(counter_1_q), .clk(in_10), .clr(and_2_out));  // open: load, D, count, carry
  Multiplexer #(.enable("false")) multiplexer_2 (
    .in0(d_ff_1_q), .in1(d_ff_2_q), .out(Actual_State), .sel(bitfinder_1_found));
  D_Flip_Flop #(.trigger("high")) d_ff_2 (.clk(in_10), .D(adder_1_out), .Q(d_ff_2_q));  // open: Qn, preset, en, reset
  BitFinder #(.width(4)) bitfinder_1 (.in(counter_2_q), .found(bitfinder_1_found));  // open: index
  Counter #(.width(4), .max('hf)) counter_2 (
    .Q(counter_2_q), .clk(in_10), .clr(and_2_out));  // open: load, D, count, carry
  and and_2 (and_2_out, clock_1_out, in_8);
  Clock clock_1 (.out(clock_1_out));

  // Notes on the sheet:
  //   State of neighber cells
  //   Born =
  //   Overcroveded >
  //   When cell gets loney <
endmodule
