// Logisim project Logika komurki.circ as structural Verilog: 1 circuit, main circuit main
module main (
  input  [3:0] When_cell_gets_alive,
  input  CLK,
  input  in_3,
  input  in_4,
  input  in_5,
  input  in_6,
  input  in_7,
  input  in_8,
  input  in_9,
  input  in_10,
  input  [3:0] When_cell_is_overcroveded,
  input  [3:0] When_cell_is_lonely,
  output Actual_State,
  output [3:0] out_14
);

  wire and_1_out, clock_1_out, comparator_1_eq, comparator_2_gt, comparator_3_lt, multiplexer_1_out,
       nor_1_out, or_1_out;

  BitAdder #(.width(1)) bitadder_1 (
    .in0(in_3), .in1(in_4), .in2(in_5), .in3(in_6), .in4(in_7), .in5(in_8), .in6(in_9), .in7(in_10),
    .out(out_14));
  Comparator #(.width(4)) comparator_1 (.a(out_14), .b(When_cell_gets_alive), .eq(comparator_1_eq));  // open: gt, lt
  Comparator #(.width(4)) comparator_2 (
    .a(out_14), .b(When_cell_is_overcroveded), .gt(comparator_2_gt));  // open: eq, lt
  Comparator #(.width(4)) comparator_3 (.a(out_14), .b(When_cell_is_lonely), .lt(comparator_3_lt));  // open: gt, eq
  and and_1 (and_1_out, comparator_1_eq, ~Actual_State);  // AND_Gate
  nor nor_1 (nor_1_out, comparator_2_gt, comparator_3_lt);
  or or_1 (or_1_out, CLK, clock_1_out);
  Multiplexer #(.enable("false")) multiplexer_1 (
    .in0(and_1_out), .in1(nor_1_out), .out(multiplexer_1_out), .sel(Actual_State));
  Clock clock_1 (.out(clock_1_out));
  D_Flip_Flop d_ff_1 (.clk(or_1_out), .D(multiplexer_1_out), .Q(Actual_State));  // open: Qn, preset, en, reset

  // Notes on the sheet:
  //   State of neighber cells
endmodule
