// Logisim project Register1x32.circ as structural Verilog: 1 circuit, main circuit main
module main (
  input  [31:0] in_1,
  input  [31:0] in_2,
  output [31:0] out_3
);

  Adder #(.width(1)) adder_1 (.a(in_1[0]), .b(in_2[0]), .out(out_3[0]));  // open: cin, cout
  Adder #(.width(1)) adder_2 (.a(in_1[1]), .b(in_2[1]), .out(out_3[1]));  // open: cin, cout
  Adder #(.width(1)) adder_3 (.a(in_1[2]), .b(in_2[2]), .out(out_3[2]));  // open: cin, cout
  Adder #(.width(1)) adder_4 (.a(in_1[3]), .b(in_2[3]), .out(out_3[3]));  // open: cin, cout
  Adder #(.width(1)) adder_5 (.a(in_1[4]), .b(in_2[4]), .out(out_3[4]));  // open: cin, cout
  Adder #(.width(1)) adder_6 (.a(in_1[5]), .b(in_2[5]), .out(out_3[5]));  // open: cin, cout
  Adder #(.width(1)) adder_7 (.a(in_1[6]), .b(in_2[6]), .out(out_3[6]));  // open: cin, cout
  Adder #(.width(1)) adder_8 (.a(in_1[7]), .b(in_2[7]), .out(out_3[7]));  // open: cin, cout
  Adder #(.width(1)) adder_9 (.a(in_1[8]), .b(in_2[8]), .out(out_3[8]));  // open: cin, cout
  Adder #(.width(1)) adder_10 (.a(in_1[9]), .b(in_2[9]), .out(out_3[9]));  // open: cin, cout
  Adder #(.width(1)) adder_11 (.a(in_1[10]), .b(in_2[10]), .out(out_3[10]));  // open: cin, cout
  Adder #(.width(1)) adder_12 (.a(in_1[11]), .b(in_2[11]), .out(out_3[11]));  // open: cin, cout
  Adder #(.width(1)) adder_13 (.a(in_1[12]), .b(in_2[12]), .out(out_3[12]));  // open: cin, cout
  Adder #(.width(1)) adder_14 (.a(in_1[13]), .b(in_2[13]), .out(out_3[13]));  // open: cin, cout
  Adder #(.width(1)) adder_15 (.a(in_1[14]), .b(in_2[14]), .out(out_3[14]));  // open: cin, cout
  Adder #(.width(1)) adder_16 (.a(in_1[15]), .b(in_2[15]), .out(out_3[15]));  // open: cin, cout
  Adder #(.width(1)) adder_17 (.a(in_1[16]), .b(in_2[16]), .out(out_3[16]));  // open: cin, cout
  Adder #(.width(1)) adder_18 (.a(in_1[17]), .b(in_2[17]), .out(out_3[17]));  // open: cin, cout
  Adder #(.width(1)) adder_19 (.a(in_1[18]), .b(in_2[18]), .out(out_3[18]));  // open: cin, cout
  Adder #(.width(1)) adder_20 (.a(in_1[19]), .b(in_2[19]), .out(out_3[19]));  // open: cin, cout
  Adder #(.width(1)) adder_21 (.a(in_1[20]), .b(in_2[20]), .out(out_3[20]));  // open: cin, cout
  Adder #(.width(1)) adder_22 (.a(in_1[21]), .b(in_2[21]), .out(out_3[21]));  // open: cin, cout
  Adder #(.width(1)) adder_23 (.a(in_1[22]), .b(in_2[22]), .out(out_3[22]));  // open: cin, cout
  Adder #(.width(1)) adder_24 (.a(in_1[23]), .b(in_2[23]), .out(out_3[23]));  // open: cin, cout
  Adder #(.width(1)) adder_25 (.a(in_1[24]), .b(in_2[24]), .out(out_3[24]));  // open: cin, cout
  Adder #(.width(1)) adder_26 (.a(in_1[25]), .b(in_2[25]), .out(out_3[25]));  // open: cin, cout
  Adder #(.width(1)) adder_27 (.a(in_1[26]), .b(in_2[26]), .out(out_3[26]));  // open: cin, cout
  Adder #(.width(1)) adder_28 (.a(in_1[27]), .b(in_2[27]), .out(out_3[27]));  // open: cin, cout
  Adder #(.width(1)) adder_29 (.a(in_1[28]), .b(in_2[28]), .out(out_3[28]));  // open: cin, cout
  Adder #(.width(1)) adder_30 (.a(in_1[29]), .b(in_2[29]), .out(out_3[29]));  // open: cin, cout
  Adder #(.width(1)) adder_31 (.a(in_1[30]), .b(in_2[30]), .out(out_3[30]));  // open: cin, cout
  Adder #(.width(1)) adder_32 (.a(in_1[31]), .b(in_2[31]), .out(out_3[31]));  // open: cin, cout
endmodule
