// Logisim project Register32x32.circ as structural Verilog: 1 circuit, main circuit main
module main (
  input  [31:0] in_1,
  input  [31:0] in_2,
  input  [31:0] in_3,
  input  [31:0] in_4,
  input  [31:0] in_5,
  input  [31:0] in_6,
  input  [31:0] in_7,
  input  [31:0] in_8,
  input  [31:0] in_9,
  input  [31:0] in_10,
  input  [31:0] in_11,
  input  [31:0] in_12,
  input  [31:0] in_13,
  input  [31:0] in_14,
  input  [31:0] in_15,
  input  [31:0] in_16,
  input  [31:0] in_17,
  input  [31:0] in_18,
  input  [31:0] in_19,
  input  [31:0] in_20,
  input  [31:0] in_21,
  input  [31:0] in_22,
  input  [31:0] in_23,
  input  [31:0] in_24,
  input  [31:0] in_25,
  input  [31:0] in_26,
  input  [31:0] in_27,
  input  [31:0] in_28,
  input  [31:0] in_29,
  input  [31:0] in_30,
  input  [31:0] in_31,
  input  [31:0] in_32,
  input  [31:0] in_33,
  input  [31:0] in_34,
  input  [31:0] in_35,
  input  [31:0] in_36,
  input  [31:0] in_37,
  input  [31:0] in_38,
  input  [31:0] in_39,
  input  [31:0] in_40,
  input  [31:0] in_41,
  input  [31:0] in_42,
  input  [31:0] in_43,
  input  [31:0] in_44,
  input  [31:0] in_45,
  input  [31:0] in_46,
  input  [31:0] in_47,
  input  [31:0] in_48,
  input  [31:0] in_49,
  input  [31:0] in_50,
  input  [31:0] in_51,
  input  [31:0] in_52,
  input  [31:0] in_53,
  input  [31:0] in_54,
  input  [31:0] in_55,
  input  [31:0] in_56,
  input  [31:0] in_57,
  input  [31:0] in_58,
  input  [31:0] in_59,
  input  [31:0] in_60,
  input  [31:0] in_61,
  input  [31:0] in_62,
  input  [31:0] in_63,
  input  [31:0] in_64,
  output [31:0] out_65,
  output [31:0] out_66,
  output [31:0] out_67,
  output [31:0] out_68,
  output [31:0] out_69,
  output [31:0] out_70,
  output [31:0] out_71,
  output [31:0] out_72,
  output [31:0] out_73,
  output [31:0] out_74,
  output [31:0] out_75,
  output [31:0] out_76,
  output [31:0] out_77,
  output [31:0] out_78,
  output [31:0] out_79,
  output [31:0] out_80,
  output [31:0] out_81,
  output [31:0] out_82,
  output [31:0] out_83,
  output [31:0] out_84,
  output [31:0] out_85,
  output [31:0] out_86,
  output [31:0] out_87,
  output [31:0] out_88,
  output [31:0] out_89,
  output [31:0] out_90,
  output [31:0] out_91,
  output [31:0] out_92,
  output [31:0] out_93,
  output [31:0] out_94,
  output [31:0] out_95,
  output [31:0] out_96
);

  Register1x32_main main_1 (.in_1(in_1), .in_2(in_33), .out_3(out_65));
  Register1x32_main main_2 (.in_1(in_2), .in_2(in_34), .out_3(out_66));
  Register1x32_main main_3 (.in_1(in_3), .in_2(in_35), .out_3(out_67));
  Register1x32_main main_4 (.in_1(in_4), .in_2(in_36), .out_3(out_68));
  Register1x32_main main_5 (.in_1(in_5), .in_2(in_37), .out_3(out_69));
  Register1x32_main main_6 (.in_1(in_6), .in_2(in_38), .out_3(out_70));
  Register1x32_main main_7 (.in_1(in_7), .in_2(in_39), .out_3(out_71));
  Register1x32_main main_8 (.in_1(in_8), .in_2(in_40), .out_3(out_72));
  Register1x32_main main_9 (.in_1(in_9), .in_2(in_41), .out_3(out_73));
  Register1x32_main main_10 (.in_1(in_10), .in_2(in_42), .out_3(out_74));
  Register1x32_main main_11 (.in_1(in_11), .in_2(in_43), .out_3(out_75));
  Register1x32_main main_12 (.in_1(in_12), .in_2(in_44), .out_3(out_76));
  Register1x32_main main_13 (.in_1(in_13), .in_2(in_45), .out_3(out_77));
  Register1x32_main main_14 (.in_1(in_14), .in_2(in_46), .out_3(out_78));
  Register1x32_main main_15 (.in_1(in_15), .in_2(in_47), .out_3(out_79));
  Register1x32_main main_16 (.in_1(in_16), .in_2(in_48), .out_3(out_80));
  Register1x32_main main_17 (.in_1(in_17), .in_2(in_49), .out_3(out_81));
  Register1x32_main main_18 (.in_1(in_18), .in_2(in_50), .out_3(out_82));
  Register1x32_main main_19 (.in_1(in_19), .in_2(in_51), .out_3(out_83));
  Register1x32_main main_20 (.in_1(in_20), .in_2(in_52), .out_3(out_84));
  Register1x32_main main_21 (.in_1(in_21), .in_2(in_53), .out_3(out_85));
  Register1x32_main main_22 (.in_1(in_22), .in_2(in_54), .out_3(out_86));
  Register1x32_main main_23 (.in_1(in_23), .in_2(in_55), .out_3(out_87));
  Register1x32_main main_24 (.in_1(in_24), .in_2(in_56), .out_3(out_88));
  Register1x32_main main_25 (.in_1(in_25), .in_2(in_57), .out_3(out_89));
  Register1x32_main main_26 (.in_1(in_26), .in_2(in_58), .out_3(out_90));
  Register1x32_main main_27 (.in_1(in_27), .in_2(in_59), .out_3(out_91));
  Register1x32_main main_28 (.in_1(in_28), .in_2(in_60), .out_3(out_92));
  Register1x32_main main_29 (.in_1(in_29), .in_2(in_61), .out_3(out_93));
  Register1x32_main main_30 (.in_1(in_30), .in_2(in_62), .out_3(out_94));
  Register1x32_main main_31 (.in_1(in_31), .in_2(in_63), .out_3(out_95));
  Register1x32_main main_32 (.in_1(in_32), .in_2(in_64), .out_3(out_96));
endmodule
