// Logisim project Uu_Down1.circ as structural Verilog: 1 circuit, main circuit main
module main (
  input  [19:0] in_1,
  input  [4:0] in_2,
  input  [4:0] in_3,
  input  in_4,
  input  in_5,
  output [19:0] out_6
);

  wire comparator_1_gt, comparator_1_lt, comparator_2_eq, comparator_2_gt, comparator_2_lt, or_1_out;
  wire [7:0] counter_1_q;

  Counter #(.max('h5a)) counter_1 (.Q(counter_1_q), .clk(in_4));  // open: load, D, count, carry, clr
  Comparator comparator_1 (.a(counter_1_q), .b(8'h37), .gt(comparator_1_gt), .lt(comparator_1_lt));  // open: eq
  Comparator #(.width(5)) comparator_2 (
    .a(in_2), .b(in_3), .gt(comparator_2_gt), .eq(comparator_2_eq), .lt(comparator_2_lt));
  or or_1 (or_1_out, comparator_1_lt, comparator_2_gt, comparator_2_lt, in_5);
  Register #(.width(20), .trigger("high")) register_1 (
    .D(in_1), .Q(out_6), .clk(comparator_2_eq), .clr(or_1_out));  // open: en
endmodule
