// Logisim project Uu_Down32.circ as structural Verilog: 1 circuit, main circuit main
module main (
  input  [4:0] in_1,
  input  [31:0] in_2,
  input  in_3,
  output [31:0] out_4,
  output [31:0] out_5,
  output [31:0] out_6,
  output [31:0] out_7,
  output [31:0] out_8,
  output [31:0] out_9,
  output [31:0] out_10,
  output [31:0] out_11,
  output [31:0] out_12,
  output [31:0] out_13,
  output [31:0] out_14,
  output [31:0] out_15,
  output [31:0] out_16,
  output [31:0] out_17,
  output [31:0] out_18,
  output [31:0] out_19,
  output [31:0] out_20,
  output [31:0] out_21,
  output [31:0] out_22,
  output [31:0] out_23,
  output [31:0] out_24,
  output [31:0] out_25,
  output [31:0] out_26,
  output [31:0] out_27,
  output [31:0] out_28,
  output [31:0] out_29,
  output [31:0] out_30,
  output [31:0] out_31,
  output [31:0] out_32,
  output [31:0] out_33,
  output [31:0] out_34,
  output [31:0] out_35
);

  // Uu_Down1_main main_1: pin names not known; wires that end beside it: in_2, in_1, {5{1'b1}}, out_4, in_3, in_3
  // Uu_Down1_main main_2: pin names not known; wires that end beside it: in_2, in_1, 5'b11110, in_3, out_5, in_3, in_3
  // Uu_Down1_main main_3: pin names not known; wires that end beside it: in_2, in_1, 5'b11101, in_3, out_6, in_3, in_3
  // Uu_Down1_main main_4: pin names not known; wires that end beside it: in_2, in_1, 5'b11100, in_3, out_7, in_3, in_3
  // Uu_Down1_main main_5: pin names not known; wires that end beside it: in_2, in_1, 5'b11011, in_3, out_8, in_3, in_3
  // Uu_Down1_main main_6: pin names not known; wires that end beside it: in_2, in_1, 5'b11010, in_3, out_9, in_3, in_3
  // Uu_Down1_main main_7: pin names not known; wires that end beside it: in_2, in_1, 5'b11001, in_3, out_10, in_3, in_3
  // Uu_Down1_main main_8: pin names not known; wires that end beside it: in_2, in_1, 5'b11000, in_3, out_11, in_3, in_3
  // Uu_Down1_main main_9: pin names not known; wires that end beside it: in_2, in_1, 5'b10111, in_3, out_12, in_3, in_3
  // Uu_Down1_main main_10: pin names not known; wires that end beside it: in_2, in_1, 5'b10110, in_3, out_13, in_3, in_3
  // Uu_Down1_main main_11: pin names not known; wires that end beside it: in_2, in_1, 5'b10101, in_3, out_14, in_3, in_3
  // Uu_Down1_main main_12: pin names not known; wires that end beside it: in_2, in_1, 5'b10100, in_3, out_15, in_3, in_3
  // Uu_Down1_main main_13: pin names not known; wires that end beside it: in_2, in_1, 5'b10011, in_3, out_16, in_3, in_3
  // Uu_Down1_main main_14: pin names not known; wires that end beside it: in_2, in_1, 5'b10010, in_3, out_17, in_3, in_3
  // Uu_Down1_main main_15: pin names not known; wires that end beside it: in_2, in_1, 5'b10001, in_3, out_18, in_3, in_3
  // Uu_Down1_main main_16: pin names not known; wires that end beside it: in_2, in_1, 5'b10000, in_3, out_19, in_3, in_3
  // Uu_Down1_main main_17: pin names not known; wires that end beside it: in_2, in_1, 5'b01111, in_3, out_20, in_3, in_3
  // Uu_Down1_main main_18: pin names not known; wires that end beside it: in_2, in_1, 5'b01110, in_3, out_21, in_3, in_3
  // Uu_Down1_main main_19: pin names not known; wires that end beside it: in_2, in_1, 5'b01101, in_3, out_22, in_3, in_3
  // Uu_Down1_main main_20: pin names not known; wires that end beside it: in_2, in_1, 5'b01100, in_3, out_23, in_3, in_3
  // Uu_Down1_main main_21: pin names not known; wires that end beside it: in_2, in_1, 5'b01011, in_3, out_24, in_3, in_3
  // Uu_Down1_main main_22: pin names not known; wires that end beside it: in_2, in_1, 5'b01010, in_3, out_25, in_3, in_3
  // Uu_Down1_main main_23: pin names not known; wires that end beside it: in_2, in_1, 5'b01001, in_3, out_26, in_3, in_3
  // Uu_Down1_main main_24: pin names not known; wires that end beside it: in_2, in_1, 5'b01000, in_3, out_27, in_3, in_3
  // Uu_Down1_main main_25: pin names not known; wires that end beside it: in_2, in_1, 5'b00111, in_3, out_28, in_3, in_3
  // Uu_Down1_main main_26: pin names not known; wires that end beside it: in_2, in_1, 5'b00110, in_3, out_29, in_3, in_3
  // Uu_Down1_main main_27: pin names not known; wires that end beside it: in_2, in_1, 5'b00101, in_3, out_30, in_3, in_3
  // Uu_Down1_main main_28: pin names not known; wires that end beside it: in_2, in_1, 5'b00100, in_3, out_31, in_3, in_3
  // Uu_Down1_main main_29: pin names not known; wires that end beside it: in_2, in_1, 5'b00011, in_3, out_32, in_3, in_3
  // Uu_Down1_main main_30: pin names not known; wires that end beside it: in_2, in_1, 5'b00010, in_3, out_33, in_3, in_3
  // Uu_Down1_main main_31: pin names not known; wires that end beside it: in_2, in_1, 5'b00001, in_3, out_34, in_3, in_3
  // Uu_Down1_main main_32: pin names not known; wires that end beside it: in_2, in_1, {5{1'b0}}, in_3, out_35, in_3
endmodule
